# Fritzing sketch analog_inputs (saved by Fritzing 0.9.4)
breadboards: 1

parts:
  R4 = Rotary Potentiometer (Small) [maximum_resistance=100kΩ package=THT]
  R6 = Rotary Potentiometer (Small) [maximum_resistance=100kΩ package=THT]
  R1 = Rotary Potentiometer (Small) [maximum_resistance=100kΩ package=THT]
  R5 = Rotary Potentiometer (Small) [maximum_resistance=100kΩ package=THT]
  R2 = Rotary Potentiometer (Small) [maximum_resistance=100kΩ package=THT]
  R3 = Rotary Potentiometer (Small) [maximum_resistance=100kΩ package=THT]
  Part1 = Arduino Uno (Rev3)

nets:
  N1: R4.leg1, R6.leg1, R1.leg1, R5.leg1, R2.leg1, R3.leg1, Part1.5V
  N2: R4.wiper, Part1.A3
  N3: R4.leg2, R6.leg2, R1.leg2, R2.leg2, R3.leg2, Part1.GND
  N4: R6.wiper, Part1.A5/SCL
  N5: R1.wiper, Part1.A0
  N6: R5.wiper, Part1.A4/SDA
  N7: R2.wiper, Part1.A1
  N8: R3.wiper, Part1.A2
