# Fritzing sketch analog_inputs2 (saved by Fritzing 0.9.4)
breadboards: 1

parts:
  R1 = Rotary Potentiometer (Small) [maximum_resistance=100kΩ package=THT]
  Part1 = Arduino Uno (Rev3)
  R2 = Photocell (LDR) [package=THT]
  J1 = Basic Force Sensing Resistor (FSR) [package=THT]
  J2 = Basic Force Sensing Resistor (FSR) [package=THT]
  R3 = Resistor [resistance=10k tolerance=±5% package=THT]
  R4 = Resistor [resistance=10k tolerance=±5% package=THT]
  R5 = Resistor [resistance=10k tolerance=±5% package=THT]

nets:
  N1: R1.leg1, Part1.5V, R2.pin_0, J1.pin_0, J2.pin_0
  N2: R1.wiper, Part1.A0
  N3: R1.leg2, Part1.A4/SDA, Part1.A5/SCL, Part1.GND, R3.Pin_1, R4.Pin_1, R5.Pin_1
  N4: Part1.A1, R2.pin_1, R5.Pin_0
  N5: Part1.A2, J1.pin_1, R3.Pin_0
  N6: Part1.A3, J2.pin_1, R4.Pin_0
