# Fritzing sketch analog_outputs (saved by Fritzing 0.9.4)
breadboards: 1

parts:
  LED1 = LED - 5mm [color="Green (570nm)" package="5 mm [THT]"]
  R1 = Resistor [tolerance=±5% resistance=220 package=THT]
  LED2 = LED - 5mm [color="Red (633nm)" package="5 mm [THT]"]
  R2 = Resistor [tolerance=±5% resistance=220 package=THT]
  Part1 = Arduino Uno (Rev3)
  LED3 = LED - 5mm [color="Blue (470nm)" package="5 mm [THT]"]
  R3 = Resistor [tolerance=±5% resistance=220 package=THT]

nets:
  N1: LED1.cathode, LED2.cathode, Part1.GND, LED3.cathode
  N2: LED1.anode, R1.Pin_0
  N3: R1.Pin_1, Part1.D10_PWM/SS
  N4: LED2.anode, R2.Pin_0
  N5: R2.Pin_1, Part1.D11_PWM/MOSI
  N6: Part1.D9_PWM, R3.Pin_1
  N7: LED3.anode, R3.Pin_0
