# Fritzing sketch sensors_and_buttons (saved by Fritzing 0.9.4)
breadboards: 1

parts:
  R4 = Rotary Potentiometer (Small) [maximum_resistance=100kΩ package=THT]
  R6 = Rotary Potentiometer (Small) [maximum_resistance=100kΩ package=THT]
  R1 = Rotary Potentiometer (Small) [maximum_resistance=100kΩ package=THT]
  R5 = Rotary Potentiometer (Small) [maximum_resistance=100kΩ package=THT]
  R2 = Rotary Potentiometer (Small) [maximum_resistance=100kΩ package=THT]
  R3 = Rotary Potentiometer (Small) [maximum_resistance=100kΩ package=THT]
  Part1 = Arduino Uno (Rev3)
  S1 = Pushbutton [package=THT]
  S2 = Pushbutton [package=THT]
  S3 = Pushbutton [package=THT]
  S4 = Pushbutton [package=THT]
  S5 = Pushbutton [package=THT]
  S6 = Pushbutton [package=THT]
  S7 = Pushbutton [package=THT]
  S9 = Pushbutton [package=THT]

nets:
  N1: R4.leg1, R6.leg1, R1.leg1, R5.leg1, R2.leg1, R3.leg1, Part1.5V
  N2: R4.wiper, Part1.A3
  N3: R4.leg2, R6.leg2, R1.leg2, R5.leg2, R2.leg2, R3.leg2, Part1.GND, S1.leg0, S2.leg1, S3.leg0, S4.leg1, S7.leg1, S9.leg0
  N4: R6.wiper, Part1.A5/SCL
  N5: R1.wiper, Part1.A0
  N6: R5.wiper, Part1.A4/SDA
  N7: R2.wiper, Part1.A1
  N8: R3.wiper, Part1.A2
  N9: Part1.D8, S9.leg1
  N10: Part1.D9_PWM, S7.leg0
  N11: Part1.D2, S1.leg1
  N12: Part1.D3_PWM, S2.leg0
  N13: Part1.D4, S3.leg1
  N14: Part1.D5_PWM, S4.leg0
  N15: Part1.D6_PWM, S5.leg1
  N16: Part1.D7, S6.leg0
  N17: S5.leg0, S6.leg1
