# Fritzing sketch servo_motors2_extPower (saved by Fritzing 0.9.4)
breadboards: 1

parts:
  Part1 = Arduino Uno (Rev3)
  J1 = Basic Servo
  J2 = Basic Servo
  Power_plug3 = Power plug

nets:
  N1: Part1.D9_PWM, J1.pulse
  N2: Part1.D10_PWM/SS, J2.pulse
  GND: Part1.GND, J1.gnd, J2.gnd, Power_plug3.GND
  VCC: J1.vcc, J2.vcc, Power_plug3.VCC

notes:
  5v Power Supply
  5v power supply
