# Fritzing sketch servo_motors2 (saved by Fritzing 0.9.4)
breadboards: 1

parts:
  J1 = Basic Servo
  J2 = Basic Servo
  Part1 = Arduino Uno (Rev3)

nets:
  GND: J1.gnd, J2.gnd, Part1.GND
  VCC: J1.vcc, J2.vcc, Part1.5V
  N1: J1.pulse, Part1.D3_PWM
  N2: J2.pulse, Part1.D9_PWM
