# Fritzing sketch servo_2motors_extPower (saved by Fritzing 0.9.4)
breadboards: 1

parts:
  Part1 = Arduino Uno (Rev3)
  J1 = Basic Servo
  J2 = Basic Servo
  Power_plug3 = Power plug

nets:
  GND: Part1.GND, J1.gnd, J2.gnd, Power_plug3.GND
  N1: Part1.D3_PWM, J1.pulse
  N2: Part1.D5_PWM, J2.pulse
  VCC: J1.vcc, J2.vcc, Power_plug3.VCC

notes:
  5v Power Supply
  5v power supply
