# Fritzing sketch multiplexing (saved by Fritzing 0.8.3b)
breadboards: 2

parts:
  Part1 = Arduino Uno (Rev3)
  IC1 = IC, DIP package, 24 pins [chip_label=IC]
  R1 = Rotary Potentiometer (Small)
  R2 = Rotary Potentiometer (Small)
  R3 = Rotary Potentiometer (Small)
  R4 = Rotary Potentiometer (Small)
  R5 = Rotary Potentiometer (Small)
  R6 = Rotary Potentiometer (Small)
  R7 = Rotary Potentiometer (Small)
  R8 = Rotary Potentiometer (Small)
  R9 = Rotary Potentiometer (Small)
  R10 = Rotary Potentiometer (Small)
  R11 = Rotary Potentiometer (Small)
  R12 = Rotary Potentiometer (Small)
  R13 = Rotary Potentiometer (Small)
  R14 = Rotary Potentiometer (Small)
  R15 = Rotary Potentiometer (Small)
  R16 = Rotary Potentiometer (Small)

nets:
  N1: Part1.A0, IC1.pin1
  N2: Part1.5V, IC1.pin24, R1.leg1, R2.leg1, R3.leg1, R4.leg1, R5.leg1, R6.leg1, R7.leg1, R8.leg1, R9.leg1, R10.leg1, R11.leg1, R12.leg1, R13.leg1, R14.leg1, R15.leg1, R16.leg1
  N3: Part1.GND, IC1.pin12, IC1.pin15, R1.leg2, R2.leg2, R3.leg2, R4.leg2, R5.leg2, R6.leg2, R7.leg2, R8.leg2, R9.leg2, R10.leg2, R11.leg2, R12.leg2, R13.leg2, R14.leg2, R15.leg2, R16.leg2
  N4: Part1.D2, IC1.pin10
  N5: Part1.D3_PWM, IC1.pin11
  N6: Part1.D4, IC1.pin14
  N7: Part1.D5_PWM, IC1.pin13
  N8: IC1.pin2, R8.wiper
  N9: IC1.pin3, R7.wiper
  N10: IC1.pin4, R6.wiper
  N11: IC1.pin5, R5.wiper
  N12: IC1.pin6, R4.wiper
  N13: IC1.pin7, R3.wiper
  N14: IC1.pin8, R2.wiper
  N15: IC1.pin9, R1.wiper
  N16: IC1.pin16, R16.wiper
  N17: IC1.pin17, R15.wiper
  N18: IC1.pin18, R14.wiper
  N19: IC1.pin19, R13.wiper
  N20: IC1.pin20, R12.wiper
  N21: IC1.pin21, R11.wiper
  N22: IC1.pin22, R10.wiper
  N23: IC1.pin23, R9.wiper
