# Fritzing sketch input_shift_registers (saved by Fritzing 0.8.3b)
breadboards: 2

parts:
  Part1 = Arduino Uno (Rev3)
  IC1 = IC, DIP package, 16 pins [chip_label=IC]
  S1 = Pushbutton [package="[THT]"]
  S2 = Pushbutton [package="[THT]"]
  S3 = Pushbutton [package="[THT]"]
  S4 = Pushbutton [package="[THT]"]
  S5 = Pushbutton [package="[THT]"]
  S6 = Pushbutton [package="[THT]"]
  S7 = Pushbutton [package="[THT]"]
  S8 = Pushbutton [package="[THT]"]
  R1 = Resistor [tolerance=±5% resistance=10k package=THT]
  R2 = Resistor [tolerance=±5% resistance=10k package=THT]
  R3 = Resistor [tolerance=±5% resistance=10k package=THT]
  R4 = Resistor [tolerance=±5% resistance=10k package=THT]
  R5 = Resistor [tolerance=±5% resistance=10k package=THT]
  R6 = Resistor [tolerance=±5% resistance=10k package=THT]
  R7 = Resistor [tolerance=±5% resistance=10k package=THT]
  R8 = Resistor [tolerance=±5% resistance=10k package=THT]

nets:
  N1: Part1.GND, IC1.pin8, IC1.pin15, S1.Pin_1, S1.Pin_2, S2.Pin_1, S2.Pin_2, S3.Pin_1, S3.Pin_2, S4.Pin_1, S4.Pin_2, S5.Pin_1, S5.Pin_2, S6.Pin_1, S6.Pin_2, S7.Pin_1, S7.Pin_2, S8.Pin_1, S8.Pin_2
  N2: Part1.D9_PWM, IC1.pin1
  N3: Part1.D12/MISO, IC1.pin9
  N4: Part1.D13/SCK, IC1.pin2
  N5: Part1.5V, IC1.pin16, R1.Pin_0, R2.Pin_0, R3.Pin_0, R4.Pin_0, R5.Pin_0, R6.Pin_0, R7.Pin_0, R8.Pin_0
  N6: IC1.pin3, S4.Pin_3, S4.Pin_4, R4.Pin_1
  N7: IC1.pin4, S3.Pin_3, S3.Pin_4, R3.Pin_1
  N8: IC1.pin5, S2.Pin_3, S2.Pin_4, R2.Pin_1
  N9: IC1.pin6, S1.Pin_3, S1.Pin_4, R1.Pin_1
  N10: IC1.pin11, S8.Pin_3, S8.Pin_4, R8.Pin_1
  N11: IC1.pin12, S7.Pin_3, S7.Pin_4, R7.Pin_1
  N12: IC1.pin13, S6.Pin_3, S6.Pin_4, R6.Pin_1
  N13: IC1.pin14, S5.Pin_3, S5.Pin_4, R5.Pin_1
