# Fritzing sketch output_shift_registers (saved by Fritzing 0.8.3b)
breadboards: 1

parts:
  Part1 = Arduino Uno (Rev3)
  U1 = 74HC595 [package="DIP16 [THT]"]
  R1 = Resistor [tolerance=±5% resistance=220 package=THT]
  R2 = Resistor [tolerance=±5% resistance=220 package=THT]
  R3 = Resistor [tolerance=±5% resistance=220 package=THT]
  R4 = Resistor [tolerance=±5% resistance=220 package=THT]
  R5 = Resistor [tolerance=±5% resistance=220 package=THT]
  R6 = Resistor [tolerance=±5% resistance=220 package=THT]
  R7 = Resistor [tolerance=±5% resistance=220 package=THT]
  R8 = Resistor [tolerance=±5% resistance=220 package=THT]
  LED1 = LED - 5mm [color="Red (633nm)" package="5 mm [THT]"]

nets:
  GND: Part1.GND, U1.GND, U1.OE, LED1.cathode
  N1: Part1.D10_PWM/SS, U1.ST_CP
  N2: Part1.D11_PWM/MOSI, U1.DS
  N3: Part1.D13/SCK, U1.SH_CP
  5V: Part1.5V, U1.MR, U1.VCC
  N4: U1.Q1, R2.Pin_1
  N5: U1.Q2, R3.Pin_1
  N6: U1.Q3, R4.Pin_1
  N7: U1.Q4, R5.Pin_1
  N8: U1.Q5, R6.Pin_0
  N9: U1.Q6, R7.Pin_0
  N10: U1.Q7, R8.Pin_0
  N11: U1.Q0, R1.Pin_1
  N12: R1.Pin_0, LED1.anode
