# Fritzing sketch multiplexing (saved by Fritzing 0.9.4)
breadboards: 2

parts:
  IC1 = IC, DIP package, 24 pins [chip_label=IC]
  R2 = Rotary Potentiometer (Small) [maximum_resistance=100kΩ package=THT]
  R5 = Rotary Potentiometer (Small) [maximum_resistance=100kΩ package=THT]
  R1 = Rotary Potentiometer (Small) [maximum_resistance=100kΩ package=THT]
  R14 = Rotary Potentiometer (Small) [maximum_resistance=100kΩ package=THT]
  R6 = Rotary Potentiometer (Small) [maximum_resistance=100kΩ package=THT]
  R9 = Rotary Potentiometer (Small) [maximum_resistance=100kΩ package=THT]
  R16 = Rotary Potentiometer (Small) [maximum_resistance=100kΩ package=THT]
  R3 = Rotary Potentiometer (Small) [maximum_resistance=100kΩ package=THT]
  R8 = Rotary Potentiometer (Small) [maximum_resistance=100kΩ package=THT]
  R4 = Rotary Potentiometer (Small) [maximum_resistance=100kΩ package=THT]
  R11 = Rotary Potentiometer (Small) [maximum_resistance=100kΩ package=THT]
  R13 = Rotary Potentiometer (Small) [maximum_resistance=100kΩ package=THT]
  R7 = Rotary Potentiometer (Small) [maximum_resistance=100kΩ package=THT]
  R10 = Rotary Potentiometer (Small) [maximum_resistance=100kΩ package=THT]
  R15 = Rotary Potentiometer (Small) [maximum_resistance=100kΩ package=THT]
  R12 = Rotary Potentiometer (Small) [maximum_resistance=100kΩ package=THT]
  Part1 = Arduino Uno (Rev3)

nets:
  N1: IC1.pin1, Part1.A0
  N2: IC1.pin2, R8.wiper
  N3: IC1.pin3, R7.wiper
  N4: IC1.pin4, R6.wiper
  N5: IC1.pin5, R5.wiper
  N6: IC1.pin6, R4.wiper
  N7: IC1.pin7, R3.wiper
  N8: IC1.pin8, R2.wiper
  N9: IC1.pin9, R1.wiper
  N10: IC1.pin10, Part1.D2
  N11: IC1.pin11, Part1.D3_PWM
  N12: IC1.pin12, IC1.pin15, R2.leg2, R5.leg2, R1.leg2, R14.leg2, R6.leg2, R9.leg2, R16.leg2, R3.leg2, R8.leg2, R4.leg2, R11.leg2, R13.leg2, R7.leg2, R10.leg2, R15.leg2, R12.leg2, Part1.GND
  N13: IC1.pin13, Part1.D5_PWM
  N14: IC1.pin14, Part1.D4
  N15: IC1.pin16, R16.wiper
  N16: IC1.pin17, R15.wiper
  N17: IC1.pin18, R14.wiper
  N18: IC1.pin19, R13.wiper
  N19: IC1.pin20, R12.wiper
  N20: IC1.pin21, R11.wiper
  N21: IC1.pin22, R10.wiper
  N22: IC1.pin23, R9.wiper
  N23: IC1.pin24, R2.leg1, R5.leg1, R1.leg1, R14.leg1, R6.leg1, R9.leg1, R16.leg1, R3.leg1, R8.leg1, R4.leg1, R11.leg1, R13.leg1, R7.leg1, R10.leg1, R15.leg1, R12.leg1, Part1.5V
