# Fritzing sketch analogIn_v2 (saved by Fritzing 0.9.3b)
breadboards: 1

parts:
  Part1 = Arduino Uno (Rev3)
  R2 = Rotary Potentiometer (Small) [maximum_resistance=100kΩ package=THT]
  R3 = Resistor [tolerance=±5% resistance=220 package=THT]
  LED1 = LED - 5mm [color="Red (633nm)" package="5 mm [THT]"]

nets:
  N1: Part1.A0, R2.wiper
  N2: Part1.GND, R2.leg2, R3.Pin_1
  N3: Part1.D2, LED1.anode
  N4: Part1.5V, R2.leg1
  N5: R3.Pin_0, LED1.cathode
