# Fritzing sketch analogOutServoEvery (saved by Fritzing 0.9.4)
breadboards: 1

parts:
  R2 = Rotary Potentiometer (Small) [maximum_resistance=100kΩ package=THT]
  J1 = Basic Servo
  Arduino_Nano_Every = Arduino Nano Every THT

nets:
  N1: R2.leg1, J1.vcc, Arduino_Nano_Every.Pin_12
  N2: R2.wiper, Arduino_Nano_Every.Pin_4
  N3: R2.leg2, J1.gnd, Arduino_Nano_Every.Pin_14, Arduino_Nano_Every.Pin_19
  N4: J1.pulse, Arduino_Nano_Every.Pin_27
  N5: Arduino_Nano_Every.Pin_13, Arduino_Nano_Every.Pin_18

custom parts:
  Arduino Nano Every THT: The Nano Every is Arduino’s 5V compatible board in the smallest available form factor: 45x18mm! The Arduino Nano is the preferred board for many projects requiring a small and easy to use microcontroller board. The small footprint and low price, make the Nano Every particularly suited for wearable inventions, low cost robotics, electronic musical instruments, and general use to control smaller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
