# Fritzing sketch analogOutSimple (saved by Fritzing 0.9.3b)
breadboards: 1

parts:
  Part1 = Arduino Uno (Rev3)
  LED = LED - 5mm [color="Red (633nm)" package="5 mm [THT]"]
  R3 = Resistor [tolerance=±5% resistance=220 package=THT]

nets:
  N1: Part1.D3_PWM, R3.Pin_1
  N2: Part1.GND, LED.cathode
  N3: LED.anode, R3.Pin_0
