# Fritzing sketch analogOutSimpleEvery (saved by Fritzing 0.9.4)
breadboards: 1

parts:
  LED = LED - 5mm [color="Red (633nm)" package="5 mm [THT]"]
  R3 = Resistor [tolerance=±5% resistance=220 package=THT]
  ArduinoNanoEvery = Arduino Nano Every THT

nets:
  N1: LED.cathode, ArduinoNanoEvery.Pin_14, ArduinoNanoEvery.Pin_19
  N2: LED.anode, R3.Pin_0
  N3: R3.Pin_1, ArduinoNanoEvery.Pin_21
  N4: ArduinoNanoEvery.Pin_13, ArduinoNanoEvery.Pin_18

custom parts:
  Arduino Nano Every THT: The Nano Every is Arduino’s 5V compatible board in the smallest available form factor: 45x18mm! The Arduino Nano is the preferred board for many projects requiring a small and easy to use microcontroller board. The small footprint and low price, make the Nano Every particularly suited for wearable inventions, low cost robotics, electronic musical instruments, and general use to control smaller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
