# Fritzing sketch digitalIn (saved by Fritzing 0.9.3b)
breadboards: 1

parts:
  Part1 = Arduino Uno (Rev3)
  LED = LED - 5mm [color="Red (633nm)" package="5 mm [THT]"]
  R2 = Resistor [tolerance=±5% resistance=220 package=THT]
  S1 = Pushbutton [package="[THT]"]
  R1 = Resistor [tolerance=±5% resistance=10k package=THT]

nets:
  N1: Part1.D13/SCK, R2.Pin_1
  N2: Part1.D2, S1.Pin_1, S1.Pin_2, R1.Pin_0
  N3: Part1.5V, S1.Pin_3, S1.Pin_4
  N4: Part1.GND, LED.cathode, R1.Pin_1
  N5: LED.anode, R2.Pin_0
