# Fritzing sketch digitalInEvery (saved by Fritzing 0.9.4)
breadboards: 1

parts:
  LED1 = LED - 5mm [color="Red (633nm)" package="5 mm [THT]"]
  S2 = Pushbutton [package="[THT]"]
  Arduino_Nano_Every = Arduino Nano Every THT
  R3 = Resistor [tolerance=±5% resistance=10k package=THT]

nets:
  N1: LED1.cathode, Arduino_Nano_Every.Pin_14, Arduino_Nano_Every.Pin_19, R3.Pin_1
  N2: LED1.anode, Arduino_Nano_Every.Pin_1
  N3: S2.Pin_1, S2.Pin_2, Arduino_Nano_Every.Pin_20, R3.Pin_0
  N4: S2.Pin_3, S2.Pin_4, Arduino_Nano_Every.Pin_12
  N5: Arduino_Nano_Every.Pin_13, Arduino_Nano_Every.Pin_18

custom parts:
  Arduino Nano Every THT: The Nano Every is Arduino’s 5V compatible board in the smallest available form factor: 45x18mm! The Arduino Nano is the preferred board for many projects requiring a small and easy to use microcontroller board. The small footprint and low price, make the Nano Every particularly suited for wearable inventions, low cost robotics, electronic musical instruments, and general use to control smaller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
