# Fritzing sketch digitalOutEvery (saved by Fritzing 0.9.4)
breadboards: 1

parts:
  LED1 = LED - 5mm [color="Red (633nm)" package="5 mm [THT]"]
  R2 = Resistor [tolerance=±5% resistance=220 package=THT]
  Arduino_Nano_Every = Arduino Nano Every THT

nets:
  N1: LED1.cathode, Arduino_Nano_Every.Pin_14, Arduino_Nano_Every.Pin_19
  N2: LED1.anode, R2.Pin_0
  N3: R2.Pin_1, Arduino_Nano_Every.Pin_1
  N4: Arduino_Nano_Every.Pin_13, Arduino_Nano_Every.Pin_18

custom parts:
  Arduino Nano Every THT: The Nano Every is Arduino’s 5V compatible board in the smallest available form factor: 45x18mm! The Arduino Nano is the preferred board for many projects requiring a small and easy to use microcontroller board. The small footprint and low price, make the Nano Every particularly suited for wearable inventions, low cost robotics, electronic musical instruments, and general use to control smaller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
