# Fritzing sketch external_led_switch (saved by Fritzing 0.9.4)
breadboards: 1

parts:
  LED = LED - 3mm [color="Red (633nm)" package="3 mm [THT]"]
  R1 = Resistor [tolerance=±5% resistance=330 package=THT]
  Mod1 = Raspberry Pi Pico
  switch = Pushbutton [package="[THT]"]

nets:
  N1: LED.cathode, Mod1.pin_3, Mod1.pin_8, Mod1.pin_13, Mod1.pin_18, Mod1.pin_23, Mod1.pin_28, Mod1.pin_33, Mod1.pin_38
  N2: LED.anode, R1.Pin_1
  N3: R1.Pin_0, Mod1.pin_20
  N4: Mod1.pin_19, switch.Pin_3, switch.Pin_4
  N5: Mod1.pin_36, switch.Pin_1, switch.Pin_2

custom parts:
  Raspberry Pi Pico: Raspberry Pi Pico. Based around the RP2040 microcontroller the Pico is a low cost microcontroller device bringing Raspberry Pi quality, cost, and easy of use to the microcontroller space. Jan 2021, Split part in to two versions: tht (this one) and SMD. This one will drill holes for a .1 in header in pcb to allow plugging in the module as well as providing pads to solder the module to the top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
