# Fritzing sketch mosfet (saved by Fritzing 0.9.4)
breadboards: 1

parts:
  PICO = Raspberry Pi Pico
  solenoid = Solenoid
  VCC = Battery block 9V
  diode = Diode [package=diode-1n4148]
  MOSFET = MOSFET-NCHANNEL [package=to220v]

nets:
  N1: PICO.pin_3, PICO.pin_8, PICO.pin_13, PICO.pin_18, PICO.pin_23, PICO.pin_28, PICO.pin_33, PICO.pin_38, solenoid.pin1, VCC.-, diode.A, MOSFET.D, MOSFET.S
  N2: PICO.pin_20, MOSFET.G
  N3: solenoid.pin2, VCC.+, diode.C

custom parts:
  Raspberry Pi Pico: Raspberry Pi Pico. Based around the RP2040 microcontroller the Pico is a low cost microcontroller device bringing Raspberry Pi quality, cost, and easy of use to the microcontroller space. Jan 2021, Split part in to two versions: tht (this one) and SMD. This one will drill holes for a .1 in header in pcb to allow plugging in the module as well as providing pads to solder the module to the top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
