# Fritzing sketch motor (saved by Fritzing 0.9.4)
breadboards: 1

parts:
  PICO1 = Raspberry Pi Pico
  R2 = Resistor [tolerance=±5% resistance=10k package=THT]
  Q1 = Basic FET P-Channel [package="D2Pak [SMD]"]  # not connected
  M1 = DC Motor  # not connected
  J1 = Basic Servo  # not connected

nets:
  N1: PICO1.pin_3, PICO1.pin_8, PICO1.pin_13, PICO1.pin_18, PICO1.pin_23, PICO1.pin_28, PICO1.pin_33, PICO1.pin_38, R2.Pin_0

custom parts:
  Raspberry Pi Pico: Raspberry Pi Pico. Based around the RP2040 microcontroller the Pico is a low cost microcontroller device bringing Raspberry Pi quality, cost, and easy of use to the microcontroller space. Jan 2021, Split part in to two versions: tht (this one) and SMD. This one will drill holes for a .1 in header in pcb to allow plugging in the module as well as providing pads to solder the module to the top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
