# Fritzing sketch potentiometer (saved by Fritzing 0.9.4)
breadboards: 1

parts:
  LED = LED - 3mm [color="Red (633nm)" package="3 mm [THT]"]
  R1 = Resistor [tolerance=±5% resistance=330 package=THT]
  POTENTIOMETER = POT [package=alps_pot]
  PICO = Raspberry Pi Pico

nets:
  N1: LED.cathode, POTENTIOMETER.A, PICO.pin_3, PICO.pin_8, PICO.pin_13, PICO.pin_18, PICO.pin_23, PICO.pin_28, PICO.pin_33, PICO.pin_38
  N2: LED.anode, R1.Pin_1
  N3: R1.Pin_0, PICO.pin_20
  N4: POTENTIOMETER.E, PICO.pin_36
  N5: POTENTIOMETER.S, PICO.pin_31

custom parts:
  Raspberry Pi Pico: Raspberry Pi Pico. Based around the RP2040 microcontroller the Pico is a low cost microcontroller device bringing Raspberry Pi quality, cost, and easy of use to the microcontroller space. Jan 2021, Split part in to two versions: tht (this one) and SMD. This one will drill holes for a .1 in header in pcb to allow plugging in the module as well as providing pads to solder the module to the top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
